// Logisim project ex4.circ as structural Verilog: 5 circuits, main circuit RotRight
module RotRight (
  input  [15:0] INPUT0,
  input  [3:0] AMOUNT,
  output [15:0] OUTPUT0
);

  wire [15:0] multiplexer_1_out, multiplexer_2_out, multiplexer_3_out, rot1_1_out_2, rot2_1_out_2,
       rot4_1_out_2, rot8_1_out_2;

  rot1 rot1_1 (.in_1(INPUT0), .out_2(rot1_1_out_2));
  Multiplexer #(.width(16)) multiplexer_1 (.in0(INPUT0), .in1(rot1_1_out_2), .out(multiplexer_1_out), .sel(AMOUNT[0]));
  rot2 rot2_1 (.in_1(multiplexer_1_out), .out_2(rot2_1_out_2));
  Multiplexer #(.width(16)) multiplexer_2 (
    .in0(multiplexer_1_out), .in1(rot2_1_out_2), .out(multiplexer_2_out), .sel(AMOUNT[1]));
  rot4 rot4_1 (.in_1(multiplexer_2_out), .out_2(rot4_1_out_2));
  Multiplexer #(.width(16)) multiplexer_3 (
    .in0(multiplexer_2_out), .in1(rot4_1_out_2), .out(multiplexer_3_out), .sel(AMOUNT[2]));
  Multiplexer #(.width(16)) multiplexer_4 (.in0(multiplexer_3_out), .in1(rot8_1_out_2), .out(OUTPUT0), .sel(AMOUNT[3]));
  rot8 rot8_1 (.in_1(multiplexer_3_out), .out_2(rot8_1_out_2));

  // Notes on the sheet:
  //   R = A > > B | A < < (16-B)
endmodule

module rot1 (
  input  [15:0] in_1,
  output [15:0] out_2
);


  assign out_2 = {in_1[0], in_1[15:1]};

  // Notes on the sheet:
  //   A > > 1 | A < < 15
endmodule

module rot2 (
  input  [15:0] in_1,
  output [15:0] out_2
);


  assign out_2 = {in_1[1:0], in_1[15:2]};

  // Notes on the sheet:
  //   A > > 2 | A < < 14
endmodule

module rot4 (
  input  [15:0] in_1,
  output [15:0] out_2
);


  assign out_2 = {in_1[3:0], in_1[15:4]};

  // Notes on the sheet:
  //   A > > 4 | A < < 12
endmodule

module rot8 (
  input  [15:0] in_1,
  output [15:0] out_2
);


  assign out_2 = {in_1[7:0], in_1[15:8]};

  // Notes on the sheet:
  //   A > > 8 | A < < 8
endmodule
