// Logisim project alu.circ as structural Verilog: 1 circuit, main circuit alu
module alu (
  input  [31:0] A,
  input  [31:0] B,
  input  [3:0] ALUSel,
  output [31:0] ALUResult
);

  wire comparator_1_lt;
  wire [31:0] add0, and7, mul8, mulh9, mulhu11, multiplexer_1_out, multiplexer_2_out, multiplexer_3_out,
       multiplexer_4_out, multiplexer_5_out, multiplexer_6_out, multiplexer_7_out, multiplexer_8_out,
       multiplexer_9_out, multiplexer_10_out, multiplexer_11_out, multiplier_2_out, multiplier_3_out, or6,
       sll1, slt2, sra13, srl5, sub12, xor4;
  wire [63:0] bit_extender_1_out, bit_extender_2_out, bit_extender_3_out, bit_extender_4_out;

  Multiplexer #(.width(32)) multiplexer_1 (.in0(add0), .in1(sll1), .out(multiplexer_1_out), .sel(ALUSel[0]));
  Multiplexer #(.width(32)) multiplexer_2 (.in0(xor4), .in1(srl5), .out(multiplexer_2_out), .sel(ALUSel[0]));
  Multiplexer #(.width(32)) multiplexer_3 (.in0(or6), .in1(and7), .out(multiplexer_3_out), .sel(ALUSel[0]));
  Multiplexer #(.width(32)) multiplexer_4 (.in0(mul8), .in1(mulh9), .out(multiplexer_4_out), .sel(ALUSel[0]));
  Multiplexer #(.width(32)) multiplexer_5 (.in0(sub12), .in1(sra13), .out(multiplexer_5_out), .sel(ALUSel[0]));
  Multiplexer #(.width(32)) multiplexer_6 (
    .in0(multiplexer_1_out), .in1(slt2), .out(multiplexer_6_out), .sel(ALUSel[1]));
  Multiplexer #(.width(32)) multiplexer_7 (
    .in0(multiplexer_2_out), .in1(multiplexer_3_out), .out(multiplexer_7_out), .sel(ALUSel[1]));
  Multiplexer #(.width(32)) multiplexer_8 (
    .in0(multiplexer_4_out), .in1(mulhu11), .out(multiplexer_8_out), .sel(ALUSel[1]));
  Multiplexer #(.width(32)) multiplexer_9 (.in0(multiplexer_5_out), .in1(B), .out(multiplexer_9_out), .sel(ALUSel[1]));
  Multiplexer #(.width(32)) multiplexer_10 (
    .in0(multiplexer_6_out), .in1(multiplexer_7_out), .out(multiplexer_10_out), .sel(ALUSel[2]));
  Multiplexer #(.width(32)) multiplexer_11 (
    .in0(multiplexer_8_out), .in1(multiplexer_9_out), .out(multiplexer_11_out), .sel(ALUSel[2]));
  Multiplexer #(.width(32)) multiplexer_12 (
    .in0(multiplexer_10_out), .in1(multiplexer_11_out), .out(ALUResult), .sel(ALUSel[3]));
  assign bit_extender_1_out = {{32{A[31]}}, A};  // Bit_Extender bit_extender_1
  assign bit_extender_2_out = {{32{B[31]}}, B};  // Bit_Extender bit_extender_2
  assign bit_extender_3_out = {{32{1'b0}}, A};  // Bit_Extender bit_extender_3
  assign bit_extender_4_out = {{32{1'b0}}, B};  // Bit_Extender bit_extender_4
  Adder #(.width(32)) adder_1 (.a(A), .b(B), .out(add0));  // open: cin, cout
  Shifter #(.width(32)) shifter_1 (.in(A), .\dist (B[4:0]), .out(sll1));
  Comparator #(.width(32)) comparator_1 (.a(A), .b(B), .lt(comparator_1_lt));  // open: gt, eq
  assign xor4 = A ^ B;  // XOR_Gate xor_1, 32 bits wide
  Shifter #(.shift("lr"), .width(32)) shifter_2 (.in(A), .\dist (B[4:0]), .out(srl5));
  assign or6 = A | B;  // OR_Gate or_1, 32 bits wide
  assign and7 = A & B;  // AND_Gate and_1, 32 bits wide
  Multiplier #(.mode("twosComplement"), .width(32)) multiplier_1 (.a(A), .b(B), .out(mul8));  // open: cin, cout
  Multiplier #(.mode("twosComplement"), .width(64)) multiplier_2 (
    .a(bit_extender_1_out), .b(bit_extender_2_out), .out({mulh9, multiplier_2_out}));  // open: cin, cout
  Multiplier #(.width(64)) multiplier_3 (
    .a(bit_extender_3_out), .b(bit_extender_4_out), .out({mulhu11, multiplier_3_out}));  // open: cin, cout
  Subtractor #(.width(32)) subtractor_1 (.a(A), .b(B), .out(sub12));  // open: bin, bout
  Shifter #(.shift("ar"), .width(32)) shifter_3 (.in(A), .\dist (B[4:0]), .out(sra13));
  assign slt2 = {{31{1'b0}}, comparator_1_lt};  // Bit_Extender bit_extender_5

  // Other names for the same wires on the sheet: sel0 = ALUSel[0]; sel1 = ALUSel[1]; sel2 = ALUSel[2];
  //   sel3 = ALUSel[3]; bsel15[31:0] = B

  // Notes on the sheet:
  //   INPUTS to your circuit
  //   DON'T CHANGE THE LOCATIONS OF THE INPUTS AND OUTPUTS!
  //   OUTPUT from your circuit
endmodule
