// Logisim project control-logic.circ as structural Verilog: 1 circuit, main circuit control_logic
module control_logic (
  input  [31:0] Instruction,
  input  BrEq,
  input  BrLt,
  output PCSel,
  output RegWEn,
  output [2:0] ImmSel,
  output BrUn,
  output ASel,
  output BSel,
  output [3:0] ALUSel,
  output MemWEn,
  output [1:0] WBSel
);

  wire and_1_out, and_15_out, and_22_out, and_23_out, and_37_out, and_38_out, and_39_out, and_40_out,
       and_41_out, and_42_out, comparator_1_eq, comparator_2_eq, comparator_3_eq, comparator_4_eq,
       comparator_5_eq, comparator_6_eq, comparator_7_eq, comparator_12_eq, comparator_13_eq,
       comparator_14_eq, comparator_15_eq, comparator_16_eq, comparator_17_eq, comparator_18_eq,
       comparator_19_eq, comparator_20_eq, comparator_21_eq, comparator_22_eq, comparator_23_eq,
       comparator_24_eq, comparator_25_eq, comparator_26_eq, comparator_27_eq, comparator_28_eq,
       comparator_29_eq, comparator_30_eq, comparator_31_eq, comparator_32_eq, comparator_33_eq,
       comparator_34_eq, comparator_35_eq, comparator_36_eq, comparator_37_eq, comparator_38_eq,
       comparator_39_eq, comparator_40_eq, comparator_41_eq, comparator_42_eq, comparator_43_eq,
       comparator_44_eq, comparator_45_eq, is_add, is_addi, is_and, is_andi, is_auipc, is_beq, is_bge,
       is_bgeu, is_blt, is_bltu, is_bne, is_jal, is_jalr, is_lb, is_lh, is_lui, is_lw, is_mul, is_mulh,
       is_mulhu, is_or, is_ori, is_sb, is_sh, is_sll, is_slli, is_slt, is_slti, is_sra, is_srai, is_srl,
       is_srli, is_sub, is_sw, is_xor, is_xori, not_1_out, not_2_out, not_3_out;
  wire [5:0] ROM_Input;
  wire [15:14] rom_1_data;

  Comparator #(.width(7)) comparator_1 (.a(7'b0010011), .b(Instruction[6:0]), .eq(comparator_1_eq));  // open: gt, lt
  Comparator #(.width(7)) comparator_2 (.a(7'b0110011), .b(Instruction[6:0]), .eq(comparator_2_eq));  // open: gt, lt
  Comparator #(.width(7)) comparator_3 (.a(7'b0000011), .b(Instruction[6:0]), .eq(comparator_3_eq));  // open: gt, lt
  Comparator #(.width(3)) comparator_4 (.a(Instruction[14:12]), .b(3'b101), .eq(comparator_4_eq));  // open: gt, lt
  Comparator #(.width(3)) comparator_5 (.a(Instruction[14:12]), .b(3'b110), .eq(comparator_5_eq));  // open: gt, lt
  Comparator #(.width(7)) comparator_6 (.a(7'b1100011), .b(Instruction[6:0]), .eq(comparator_6_eq));  // open: gt, lt
  Comparator #(.width(7)) comparator_7 (.a(7'b0100011), .b(Instruction[6:0]), .eq(comparator_7_eq));  // open: gt, lt
  Comparator #(.width(7)) comparator_8 (.a(7'b1101111), .b(Instruction[6:0]), .eq(is_jal));  // open: gt, lt
  Comparator #(.width(7)) comparator_9 (.a(7'b1100111), .b(Instruction[6:0]), .eq(is_jalr));  // open: gt, lt
  Comparator #(.width(7)) comparator_10 (.a(7'b0010111), .b(Instruction[6:0]), .eq(is_auipc));  // open: gt, lt
  Comparator #(.width(7)) comparator_11 (.a(7'b0110111), .b(Instruction[6:0]), .eq(is_lui));  // open: gt, lt
  and and_1 (and_1_out, comparator_4_eq, comparator_1_eq);
  Comparator #(.width(3)) comparator_12 (.a(Instruction[14:12]), .b(3'b000), .eq(comparator_12_eq));  // open: gt, lt
  Comparator #(.width(3)) comparator_13 (.a(Instruction[14:12]), .b(3'b111), .eq(comparator_13_eq));  // open: gt, lt
  Comparator #(.width(3)) comparator_14 (.a(Instruction[14:12]), .b(3'b110), .eq(comparator_14_eq));  // open: gt, lt
  Comparator #(.width(3)) comparator_15 (.a(Instruction[14:12]), .b(3'b100), .eq(comparator_15_eq));  // open: gt, lt
  Comparator #(.width(3)) comparator_16 (.a(Instruction[14:12]), .b(3'b010), .eq(comparator_16_eq));  // open: gt, lt
  Comparator #(.width(3)) comparator_17 (.a(Instruction[14:12]), .b(3'b001), .eq(comparator_17_eq));  // open: gt, lt
  Comparator #(.width(3)) comparator_18 (.a(Instruction[14:12]), .b(3'b000), .eq(comparator_18_eq));  // open: gt, lt
  Comparator #(.width(3)) comparator_19 (.a(Instruction[14:12]), .b(3'b001), .eq(comparator_19_eq));  // open: gt, lt
  Comparator #(.width(3)) comparator_20 (.a(Instruction[14:12]), .b(3'b010), .eq(comparator_20_eq));  // open: gt, lt
  Comparator #(.width(3)) comparator_21 (.a(Instruction[14:12]), .b(3'b011), .eq(comparator_21_eq));  // open: gt, lt
  Comparator #(.width(3)) comparator_22 (.a(Instruction[14:12]), .b(3'b100), .eq(comparator_22_eq));  // open: gt, lt
  Comparator #(.width(3)) comparator_23 (.a(Instruction[14:12]), .b(3'b101), .eq(comparator_23_eq));  // open: gt, lt
  Comparator #(.width(3)) comparator_24 (.a(Instruction[14:12]), .b(3'b111), .eq(comparator_24_eq));  // open: gt, lt
  ROM #(.addrWidth(6), .dataWidth(16)) rom_1 (
    .addr(ROM_Input), .data({rom_1_data, WBSel, MemWEn, ALUSel, BSel, ASel, BrUn, ImmSel, RegWEn}));
  and and_2 (is_slt, comparator_2_eq, comparator_20_eq);
  and and_3 (is_mulhu, comparator_2_eq, comparator_21_eq);
  and and_4 (is_xor, comparator_2_eq, comparator_22_eq);
  and and_5 (is_or, comparator_2_eq, comparator_5_eq);
  and and_6 (is_and, comparator_2_eq, comparator_24_eq);
  Comparator #(.width(3)) comparator_25 (.a(Instruction[14:12]), .b(3'b000), .eq(comparator_25_eq));  // open: gt, lt
  Comparator #(.width(3)) comparator_26 (.a(Instruction[14:12]), .b(3'b001), .eq(comparator_26_eq));  // open: gt, lt
  Comparator #(.width(7)) comparator_27 (.a(Instruction[31:25]), .b({7{1'b0}}), .eq(comparator_27_eq));  // open: gt, lt
  Comparator #(.width(7)) comparator_28 (
    .a(Instruction[31:25]), .b(7'b0100000), .eq(comparator_28_eq));  // open: gt, lt
  and and_7 (is_addi, comparator_12_eq, comparator_1_eq);
  and and_8 (is_andi, comparator_1_eq, comparator_13_eq);
  and and_9 (is_ori, comparator_1_eq, comparator_14_eq);
  and and_10 (is_xori, comparator_1_eq, comparator_15_eq);
  and and_11 (is_slti, comparator_1_eq, comparator_16_eq);
  and and_12 (is_slli, comparator_1_eq, comparator_17_eq);
  Comparator #(.width(3)) comparator_29 (.a(Instruction[14:12]), .b(3'b100), .eq(comparator_29_eq));  // open: gt, lt
  Comparator #(.width(3)) comparator_30 (.a(Instruction[14:12]), .b(3'b101), .eq(comparator_30_eq));  // open: gt, lt
  Comparator #(.width(3)) comparator_31 (.a(Instruction[14:12]), .b(3'b110), .eq(comparator_31_eq));  // open: gt, lt
  Comparator #(.width(3)) comparator_32 (.a(Instruction[14:12]), .b(3'b111), .eq(comparator_32_eq));  // open: gt, lt
  and and_13 (is_srli, comparator_27_eq, and_1_out);
  and and_14 (is_srai, comparator_28_eq, and_1_out);
  and and_15 (and_15_out, comparator_18_eq, comparator_2_eq);
  and and_16 (is_beq, comparator_25_eq, comparator_6_eq);
  and and_17 (is_bne, comparator_26_eq, comparator_6_eq);
  and and_18 (is_blt, comparator_29_eq, comparator_6_eq);
  and and_19 (is_bge, comparator_30_eq, comparator_6_eq);
  and and_20 (is_bltu, comparator_31_eq, comparator_6_eq);
  and and_21 (is_bgeu, comparator_32_eq, comparator_6_eq);
  Comparator #(.width(3)) comparator_33 (.a(Instruction[14:12]), .b(3'b000), .eq(comparator_33_eq));  // open: gt, lt
  Comparator #(.width(3)) comparator_34 (.a(Instruction[14:12]), .b(3'b001), .eq(comparator_34_eq));  // open: gt, lt
  Comparator #(.width(3)) comparator_35 (.a(Instruction[14:12]), .b(3'b010), .eq(comparator_35_eq));  // open: gt, lt
  Comparator #(.width(3)) comparator_36 (.a(Instruction[14:12]), .b(3'b000), .eq(comparator_36_eq));  // open: gt, lt
  Comparator #(.width(3)) comparator_37 (.a(Instruction[14:12]), .b(3'b001), .eq(comparator_37_eq));  // open: gt, lt
  Comparator #(.width(3)) comparator_38 (.a(Instruction[14:12]), .b(3'b010), .eq(comparator_38_eq));  // open: gt, lt
  and and_22 (and_22_out, comparator_2_eq, comparator_19_eq);
  and and_23 (and_23_out, comparator_2_eq, comparator_23_eq);
  and and_24 (is_lb, comparator_33_eq, comparator_3_eq);
  and and_25 (is_lh, comparator_34_eq, comparator_3_eq);
  and and_26 (is_lw, comparator_35_eq, comparator_3_eq);
  and and_27 (is_sb, comparator_36_eq, comparator_7_eq);
  and and_28 (is_sh, comparator_37_eq, comparator_7_eq);
  and and_29 (is_sw, comparator_38_eq, comparator_7_eq);
  Comparator #(.width(7)) comparator_39 (.a(Instruction[31:25]), .b({7{1'b0}}), .eq(comparator_39_eq));  // open: gt, lt
  Comparator #(.width(7)) comparator_40 (
    .a(Instruction[31:25]), .b(7'b0100000), .eq(comparator_40_eq));  // open: gt, lt
  Comparator #(.width(7)) comparator_41 (
    .a(Instruction[31:25]), .b(7'b0000001), .eq(comparator_41_eq));  // open: gt, lt
  Comparator #(.width(7)) comparator_42 (.a(Instruction[31:25]), .b({7{1'b0}}), .eq(comparator_42_eq));  // open: gt, lt
  Comparator #(.width(7)) comparator_43 (
    .a(Instruction[31:25]), .b(7'b0000001), .eq(comparator_43_eq));  // open: gt, lt
  Comparator #(.width(7)) comparator_44 (.a(Instruction[31:25]), .b({7{1'b0}}), .eq(comparator_44_eq));  // open: gt, lt
  Comparator #(.width(7)) comparator_45 (
    .a(Instruction[31:25]), .b(7'b0100000), .eq(comparator_45_eq));  // open: gt, lt
  and and_30 (is_add, comparator_39_eq, and_15_out);
  and and_31 (is_sub, comparator_40_eq, and_15_out);
  and and_32 (is_mul, comparator_41_eq, and_15_out);
  and and_33 (is_sll, comparator_42_eq, and_22_out);
  and and_34 (is_mulh, comparator_43_eq, and_22_out);
  and and_35 (is_srl, comparator_44_eq, and_23_out);
  and and_36 (is_sra, comparator_45_eq, and_23_out);
  Priority_Encoder #(.select_enc(6)) priority_encoder_1 (
    .in0(is_add), .in1(is_mul), .in2(is_sub), .in3(is_sll), .in4(is_mulh), .in5(is_mulhu), .in6(is_slt),
    .in7(is_xor), .in8(is_srl), .in9(is_sra), .in10(is_or), .in11(is_and), .in12(is_lb), .in13(is_lh),
    .in14(is_lw), .in15(is_addi), .in16(is_slli), .in17(is_slti), .in18(is_xori), .in19(is_srli),
    .in20(is_srai), .in21(is_ori), .in22(is_andi), .in23(is_sb), .in24(is_sh), .in25(is_sw), .in26(is_beq),
    .in27(is_bne), .in28(is_blt), .in29(is_bge), .in30(is_bltu), .in31(is_bgeu), .in32(is_auipc),
    .in33(is_lui), .in34(is_jal), .in35(is_jalr), .out(ROM_Input));  // open: in36, in37, in38, in39, in40, in41, in42, in43, in44, in45, in46, in47, in48, in49, in50, in51, in52, in53, in54, in55, in56, in57, in58, in59, in60, in61, in62, in63, gs, en_out, en_in
  not not_1 (not_1_out, BrEq);
  not not_2 (not_2_out, BrLt);
  not not_3 (not_3_out, BrLt);
  and and_37 (and_37_out, is_beq, BrEq);
  and and_38 (and_38_out, is_bne, not_1_out);
  and and_39 (and_39_out, is_blt, BrLt);
  and and_40 (and_40_out, is_bge, not_2_out);
  and and_41 (and_41_out, is_bltu, BrLt);
  and and_42 (and_42_out, is_bgeu, not_3_out);
  or or_1 (PCSel, and_37_out, and_38_out, and_39_out, and_40_out, and_41_out, and_42_out, is_jal, is_jalr);

  // Other names for the same wires on the sheet: opcode[6:0] = Instruction[6:0]; funct3[2:0] = Instruction[14:12];
  //   funct7[6:0] = Instruction[31:25]

  // Notes on the sheet:
  //   INPUTS to your circuit
  //   contents of rom_1 (hex, n*v repeats v):
  //   1001 1401 1601 1081 1481 1581 1101 1201 1281 1681 1301 1381 41 41 41 1041 10c1 1141 1241 12c1 16c1
  //   1341 13c1 1842 1842 1842 4*1064 1074 1074 1067 17c7 2069 2041
  //   ROM FOR CONTROL LOGIC
  //   DON'T CHANGE THE LOCATIONS OF THE INPUTS AND OUTPUTS!
  //   This is only if you choose to do the ROM option
  //   OUTPUT from your circuit
  //   Reminder: If using ROM, use combinational logic for PCSel
endmodule
