// Logisim project regfile.circ as structural Verilog: 1 circuit, main circuit regfile
module regfile (
  input  [4:0] ReadIndex1,
  input  [4:0] ReadIndex2,
  input  [4:0] WriteIndex,
  input  [31:0] WriteData,
  input  RegWEn,
  input  clk,
  output [31:0] ra,
  output [31:0] sp,
  output [31:0] t0,
  output [31:0] t1,
  output [31:0] t2,
  output [31:0] s0,
  output [31:0] s1,
  output [31:0] a0,
  output [31:0] ReadData1,
  output [31:0] ReadData2
);

  wire demultiplexer_1_out0, demultiplexer_1_out1, demultiplexer_2_out0, demultiplexer_2_out1,
       demultiplexer_3_out0, demultiplexer_3_out1, demultiplexer_4_out0, demultiplexer_4_out1,
       demultiplexer_5_out0, demultiplexer_5_out1, demultiplexer_6_out0, demultiplexer_6_out1,
       demultiplexer_7_out0, demultiplexer_7_out1, demultiplexer_8_out0, demultiplexer_8_out1,
       demultiplexer_9_out0, demultiplexer_9_out1, demultiplexer_10_out0, demultiplexer_10_out1,
       demultiplexer_11_out0, demultiplexer_11_out1, demultiplexer_12_out0, demultiplexer_12_out1,
       demultiplexer_13_out0, demultiplexer_13_out1, demultiplexer_14_out0, demultiplexer_14_out1,
       demultiplexer_15_out0, demultiplexer_15_out1, WS0, WS1, WS2, WS3, WS4, WS5, WS6, WS7, WS8, WS9, WS10,
       WS11, WS12, WS13, WS14, WS15, WS16, WS17, WS18, WS19, WS20, WS21, WS22, WS23, WS24, WS25, WS26, WS27,
       WS28, WS29, WS30, WS31;
  wire [31:0] multiplexer_1_out, multiplexer_2_out, multiplexer_3_out, multiplexer_4_out, multiplexer_5_out,
       multiplexer_6_out, multiplexer_7_out, multiplexer_8_out, multiplexer_9_out, multiplexer_10_out,
       multiplexer_11_out, multiplexer_12_out, multiplexer_13_out, multiplexer_14_out, multiplexer_15_out,
       multiplexer_16_out, multiplexer_17_out, multiplexer_18_out, multiplexer_19_out, multiplexer_20_out,
       multiplexer_21_out, multiplexer_22_out, multiplexer_23_out, multiplexer_24_out, multiplexer_25_out,
       multiplexer_26_out, multiplexer_27_out, multiplexer_28_out, multiplexer_29_out, multiplexer_30_out,
       multiplexer_31_out, multiplexer_32_out, multiplexer_33_out, multiplexer_34_out, multiplexer_35_out,
       multiplexer_36_out, multiplexer_37_out, multiplexer_38_out, multiplexer_39_out, multiplexer_40_out,
       multiplexer_41_out, multiplexer_42_out, multiplexer_43_out, multiplexer_44_out, multiplexer_45_out,
       multiplexer_46_out, multiplexer_47_out, multiplexer_48_out, multiplexer_49_out, multiplexer_50_out,
       multiplexer_51_out, multiplexer_52_out, multiplexer_53_out, multiplexer_54_out, multiplexer_55_out,
       multiplexer_56_out, multiplexer_57_out, multiplexer_58_out, multiplexer_59_out, multiplexer_60_out,
       x0, x3, x4, x11, x12, x13, x14, x15, x16, x17, x18, x19, x20, x21, x22, x23, x24, x25, x26, x27, x28,
       x29, x30, x31;

  Register #(.width(32)) u_x0 (.D({32{1'b0}}), .en(WS0), .clk(clk), .Q(x0));  // open: clr
  Register #(.width(32)) x1 (.D(WriteData), .en(WS1), .clk(clk), .Q(ra));  // open: clr
  Register #(.width(32)) x2 (.D(WriteData), .en(WS2), .clk(clk), .Q(sp));  // open: clr
  Register #(.width(32)) u_x3 (.D(WriteData), .en(WS3), .clk(clk), .Q(x3));  // open: clr
  Register #(.width(32)) u_x4 (.D(WriteData), .en(WS4), .clk(clk), .Q(x4));  // open: clr
  Register #(.width(32)) x5 (.D(WriteData), .en(WS5), .clk(clk), .Q(t0));  // open: clr
  Register #(.width(32)) x6 (.D(WriteData), .en(WS6), .clk(clk), .Q(t1));  // open: clr
  Register #(.width(32)) x7 (.D(WriteData), .en(WS7), .clk(clk), .Q(t2));  // open: clr
  Register #(.width(32)) x8 (.D(WriteData), .en(WS8), .clk(clk), .Q(s0));  // open: clr
  Register #(.width(32)) x9 (.D(WriteData), .en(WS9), .clk(clk), .Q(s1));  // open: clr
  Register #(.width(32)) x10 (.D(WriteData), .en(WS10), .clk(clk), .Q(a0));  // open: clr
  Register #(.width(32)) u_x11 (.D(WriteData), .en(WS11), .clk(clk), .Q(x11));  // open: clr
  Register #(.width(32)) u_x12 (.D(WriteData), .en(WS12), .clk(clk), .Q(x12));  // open: clr
  Register #(.width(32)) u_x13 (.D(WriteData), .en(WS13), .clk(clk), .Q(x13));  // open: clr
  Register #(.width(32)) u_x14 (.D(WriteData), .en(WS14), .clk(clk), .Q(x14));  // open: clr
  Register #(.width(32)) u_x15 (.D(WriteData), .en(WS15), .clk(clk), .Q(x15));  // open: clr
  Register #(.width(32)) u_x16 (.D(WriteData), .en(WS16), .clk(clk), .Q(x16));  // open: clr
  Register #(.width(32)) u_x17 (.D(WriteData), .en(WS17), .clk(clk), .Q(x17));  // open: clr
  Register #(.width(32)) u_x18 (.D(WriteData), .en(WS18), .clk(clk), .Q(x18));  // open: clr
  Register #(.width(32)) u_x19 (.D(WriteData), .en(WS19), .clk(clk), .Q(x19));  // open: clr
  Register #(.width(32)) u_x20 (.D(WriteData), .en(WS20), .clk(clk), .Q(x20));  // open: clr
  Register #(.width(32)) u_x21 (.D(WriteData), .en(WS21), .clk(clk), .Q(x21));  // open: clr
  Register #(.width(32)) u_x22 (.D(WriteData), .en(WS22), .clk(clk), .Q(x22));  // open: clr
  Register #(.width(32)) u_x23 (.D(WriteData), .en(WS23), .clk(clk), .Q(x23));  // open: clr
  Register #(.width(32)) u_x24 (.D(WriteData), .en(WS24), .clk(clk), .Q(x24));  // open: clr
  Register #(.width(32)) u_x25 (.D(WriteData), .en(WS25), .clk(clk), .Q(x25));  // open: clr
  Register #(.width(32)) u_x26 (.D(WriteData), .en(WS26), .clk(clk), .Q(x26));  // open: clr
  Register #(.width(32)) u_x27 (.D(WriteData), .en(WS27), .clk(clk), .Q(x27));  // open: clr
  Register #(.width(32)) u_x28 (.D(WriteData), .en(WS28), .clk(clk), .Q(x28));  // open: clr
  Register #(.width(32)) u_x29 (.D(WriteData), .en(WS29), .clk(clk), .Q(x29));  // open: clr
  Register #(.width(32)) u_x30 (.D(WriteData), .en(WS30), .clk(clk), .Q(x30));  // open: clr
  Register #(.width(32)) u_x31 (.D(WriteData), .en(WS31), .clk(clk), .Q(x31));  // open: clr
  Demultiplexer demultiplexer_1 (
    .out0(demultiplexer_1_out0), .out1(demultiplexer_1_out1), .in(RegWEn), .sel(WriteIndex[4]));
  Demultiplexer demultiplexer_2 (
    .out0(demultiplexer_2_out0), .out1(demultiplexer_2_out1), .in(demultiplexer_1_out0), .sel(WriteIndex[3]));
  Demultiplexer demultiplexer_3 (
    .out0(demultiplexer_3_out0), .out1(demultiplexer_3_out1), .in(demultiplexer_1_out1), .sel(WriteIndex[3]));
  Multiplexer #(.width(32)) multiplexer_1 (.in0(x0), .in1(ra), .out(multiplexer_1_out), .sel(ReadIndex1[0]));
  Multiplexer #(.width(32)) multiplexer_2 (.in0(sp), .in1(x3), .out(multiplexer_2_out), .sel(ReadIndex1[0]));
  Multiplexer #(.width(32)) multiplexer_3 (.in0(x4), .in1(t0), .out(multiplexer_3_out), .sel(ReadIndex1[0]));
  Multiplexer #(.width(32)) multiplexer_4 (.in0(t1), .in1(t2), .out(multiplexer_4_out), .sel(ReadIndex1[0]));
  Multiplexer #(.width(32)) multiplexer_5 (.in0(s0), .in1(s1), .out(multiplexer_5_out), .sel(ReadIndex1[0]));
  Multiplexer #(.width(32)) multiplexer_6 (.in0(a0), .in1(x11), .out(multiplexer_6_out), .sel(ReadIndex1[0]));
  Multiplexer #(.width(32)) multiplexer_7 (.in0(x12), .in1(x13), .out(multiplexer_7_out), .sel(ReadIndex1[0]));
  Multiplexer #(.width(32)) multiplexer_8 (.in0(x14), .in1(x15), .out(multiplexer_8_out), .sel(ReadIndex1[0]));
  Multiplexer #(.width(32)) multiplexer_9 (.in0(x16), .in1(x17), .out(multiplexer_9_out), .sel(ReadIndex1[0]));
  Multiplexer #(.width(32)) multiplexer_10 (.in0(x18), .in1(x19), .out(multiplexer_10_out), .sel(ReadIndex1[0]));
  Multiplexer #(.width(32)) multiplexer_11 (.in0(x20), .in1(x21), .out(multiplexer_11_out), .sel(ReadIndex1[0]));
  Multiplexer #(.width(32)) multiplexer_12 (.in0(x22), .in1(x23), .out(multiplexer_12_out), .sel(ReadIndex1[0]));
  Multiplexer #(.width(32)) multiplexer_13 (.in0(x24), .in1(x25), .out(multiplexer_13_out), .sel(ReadIndex1[0]));
  Multiplexer #(.width(32)) multiplexer_14 (.in0(x26), .in1(x27), .out(multiplexer_14_out), .sel(ReadIndex1[0]));
  Multiplexer #(.width(32)) multiplexer_15 (.in0(x28), .in1(x29), .out(multiplexer_15_out), .sel(ReadIndex1[0]));
  Multiplexer #(.width(32)) multiplexer_16 (.in0(x30), .in1(x31), .out(multiplexer_16_out), .sel(ReadIndex1[0]));
  Multiplexer #(.width(32)) multiplexer_17 (.in0(x0), .in1(ra), .out(multiplexer_17_out), .sel(ReadIndex2[0]));
  Multiplexer #(.width(32)) multiplexer_18 (.in0(sp), .in1(x3), .out(multiplexer_18_out), .sel(ReadIndex2[0]));
  Multiplexer #(.width(32)) multiplexer_19 (.in0(x4), .in1(t0), .out(multiplexer_19_out), .sel(ReadIndex2[0]));
  Multiplexer #(.width(32)) multiplexer_20 (.in0(t1), .in1(t2), .out(multiplexer_20_out), .sel(ReadIndex2[0]));
  Multiplexer #(.width(32)) multiplexer_21 (.in0(s0), .in1(s1), .out(multiplexer_21_out), .sel(ReadIndex2[0]));
  Multiplexer #(.width(32)) multiplexer_22 (.in0(a0), .in1(x11), .out(multiplexer_22_out), .sel(ReadIndex2[0]));
  Multiplexer #(.width(32)) multiplexer_23 (.in0(x12), .in1(x13), .out(multiplexer_23_out), .sel(ReadIndex2[0]));
  Multiplexer #(.width(32)) multiplexer_24 (.in0(x14), .in1(x15), .out(multiplexer_24_out), .sel(ReadIndex2[0]));
  Multiplexer #(.width(32)) multiplexer_25 (.in0(x16), .in1(x17), .out(multiplexer_25_out), .sel(ReadIndex2[0]));
  Multiplexer #(.width(32)) multiplexer_26 (.in0(x18), .in1(x19), .out(multiplexer_26_out), .sel(ReadIndex2[0]));
  Multiplexer #(.width(32)) multiplexer_27 (.in0(x20), .in1(x21), .out(multiplexer_27_out), .sel(ReadIndex2[0]));
  Multiplexer #(.width(32)) multiplexer_28 (.in0(x22), .in1(x23), .out(multiplexer_28_out), .sel(ReadIndex2[0]));
  Multiplexer #(.width(32)) multiplexer_29 (.in0(x24), .in1(x25), .out(multiplexer_29_out), .sel(ReadIndex2[0]));
  Multiplexer #(.width(32)) multiplexer_30 (.in0(x26), .in1(x27), .out(multiplexer_30_out), .sel(ReadIndex2[0]));
  Multiplexer #(.width(32)) multiplexer_31 (.in0(x28), .in1(x29), .out(multiplexer_31_out), .sel(ReadIndex2[0]));
  Multiplexer #(.width(32)) multiplexer_32 (.in0(x30), .in1(x31), .out(multiplexer_32_out), .sel(ReadIndex2[0]));
  Multiplexer #(.width(32)) multiplexer_33 (
    .in0(multiplexer_3_out), .in1(multiplexer_4_out), .out(multiplexer_33_out), .sel(ReadIndex1[1]));
  Multiplexer #(.width(32)) multiplexer_34 (
    .in0(multiplexer_11_out), .in1(multiplexer_12_out), .out(multiplexer_34_out), .sel(ReadIndex1[1]));
  Multiplexer #(.width(32)) multiplexer_35 (
    .in0(multiplexer_19_out), .in1(multiplexer_20_out), .out(multiplexer_35_out), .sel(ReadIndex2[1]));
  Multiplexer #(.width(32)) multiplexer_36 (
    .in0(multiplexer_21_out), .in1(multiplexer_22_out), .out(multiplexer_36_out), .sel(ReadIndex2[1]));
  Multiplexer #(.width(32)) multiplexer_37 (
    .in0(multiplexer_23_out), .in1(multiplexer_24_out), .out(multiplexer_37_out), .sel(ReadIndex2[1]));
  Multiplexer #(.width(32)) multiplexer_38 (
    .in0(multiplexer_25_out), .in1(multiplexer_26_out), .out(multiplexer_38_out), .sel(ReadIndex2[1]));
  Multiplexer #(.width(32)) multiplexer_39 (
    .in0(multiplexer_27_out), .in1(multiplexer_28_out), .out(multiplexer_39_out), .sel(ReadIndex2[1]));
  Multiplexer #(.width(32)) multiplexer_40 (
    .in0(multiplexer_29_out), .in1(multiplexer_30_out), .out(multiplexer_40_out), .sel(ReadIndex2[1]));
  Multiplexer #(.width(32)) multiplexer_41 (
    .in0(multiplexer_31_out), .in1(multiplexer_32_out), .out(multiplexer_41_out), .sel(ReadIndex2[1]));
  Demultiplexer demultiplexer_4 (
    .out0(demultiplexer_4_out0), .out1(demultiplexer_4_out1), .in(demultiplexer_2_out0), .sel(WriteIndex[2]));
  Demultiplexer demultiplexer_5 (
    .out0(demultiplexer_5_out0), .out1(demultiplexer_5_out1), .in(demultiplexer_2_out1), .sel(WriteIndex[2]));
  Demultiplexer demultiplexer_6 (
    .out0(demultiplexer_6_out0), .out1(demultiplexer_6_out1), .in(demultiplexer_3_out0), .sel(WriteIndex[2]));
  Demultiplexer demultiplexer_7 (
    .out0(demultiplexer_7_out0), .out1(demultiplexer_7_out1), .in(demultiplexer_3_out1), .sel(WriteIndex[2]));
  Multiplexer #(.width(32)) multiplexer_42 (
    .in0(multiplexer_1_out), .in1(multiplexer_2_out), .out(multiplexer_42_out), .sel(ReadIndex1[1]));
  Multiplexer #(.width(32)) multiplexer_43 (
    .in0(multiplexer_5_out), .in1(multiplexer_6_out), .out(multiplexer_43_out), .sel(ReadIndex1[1]));
  Multiplexer #(.width(32)) multiplexer_44 (
    .in0(multiplexer_7_out), .in1(multiplexer_8_out), .out(multiplexer_44_out), .sel(ReadIndex1[1]));
  Multiplexer #(.width(32)) multiplexer_45 (
    .in0(multiplexer_9_out), .in1(multiplexer_10_out), .out(multiplexer_45_out), .sel(ReadIndex1[1]));
  Multiplexer #(.width(32)) multiplexer_46 (
    .in0(multiplexer_13_out), .in1(multiplexer_14_out), .out(multiplexer_46_out), .sel(ReadIndex1[1]));
  Multiplexer #(.width(32)) multiplexer_47 (
    .in0(multiplexer_15_out), .in1(multiplexer_16_out), .out(multiplexer_47_out), .sel(ReadIndex1[1]));
  Multiplexer #(.width(32)) multiplexer_48 (
    .in0(multiplexer_17_out), .in1(multiplexer_18_out), .out(multiplexer_48_out), .sel(ReadIndex2[1]));
  Multiplexer #(.width(32)) multiplexer_49 (
    .in0(multiplexer_42_out), .in1(multiplexer_33_out), .out(multiplexer_49_out), .sel(ReadIndex1[2]));
  Multiplexer #(.width(32)) multiplexer_50 (
    .in0(multiplexer_43_out), .in1(multiplexer_44_out), .out(multiplexer_50_out), .sel(ReadIndex1[2]));
  Multiplexer #(.width(32)) multiplexer_51 (
    .in0(multiplexer_45_out), .in1(multiplexer_34_out), .out(multiplexer_51_out), .sel(ReadIndex1[2]));
  Multiplexer #(.width(32)) multiplexer_52 (
    .in0(multiplexer_46_out), .in1(multiplexer_47_out), .out(multiplexer_52_out), .sel(ReadIndex1[2]));
  Multiplexer #(.width(32)) multiplexer_53 (
    .in0(multiplexer_48_out), .in1(multiplexer_35_out), .out(multiplexer_53_out), .sel(ReadIndex2[2]));
  Multiplexer #(.width(32)) multiplexer_54 (
    .in0(multiplexer_36_out), .in1(multiplexer_37_out), .out(multiplexer_54_out), .sel(ReadIndex2[2]));
  Multiplexer #(.width(32)) multiplexer_55 (
    .in0(multiplexer_38_out), .in1(multiplexer_39_out), .out(multiplexer_55_out), .sel(ReadIndex2[2]));
  Multiplexer #(.width(32)) multiplexer_56 (
    .in0(multiplexer_40_out), .in1(multiplexer_41_out), .out(multiplexer_56_out), .sel(ReadIndex2[2]));
  Demultiplexer demultiplexer_8 (
    .out0(demultiplexer_8_out0), .out1(demultiplexer_8_out1), .in(demultiplexer_4_out0), .sel(WriteIndex[1]));
  Demultiplexer demultiplexer_9 (
    .out0(demultiplexer_9_out0), .out1(demultiplexer_9_out1), .in(demultiplexer_4_out1), .sel(WriteIndex[1]));
  Demultiplexer demultiplexer_10 (
    .out0(demultiplexer_10_out0), .out1(demultiplexer_10_out1), .in(demultiplexer_5_out0), .sel(WriteIndex[1]));
  Demultiplexer demultiplexer_11 (
    .out0(demultiplexer_11_out0), .out1(demultiplexer_11_out1), .in(demultiplexer_5_out1), .sel(WriteIndex[1]));
  Demultiplexer demultiplexer_12 (
    .out0(demultiplexer_12_out0), .out1(demultiplexer_12_out1), .in(demultiplexer_6_out0), .sel(WriteIndex[1]));
  Demultiplexer demultiplexer_13 (
    .out0(demultiplexer_13_out0), .out1(demultiplexer_13_out1), .in(demultiplexer_6_out1), .sel(WriteIndex[1]));
  Demultiplexer demultiplexer_14 (
    .out0(demultiplexer_14_out0), .out1(demultiplexer_14_out1), .in(demultiplexer_7_out0), .sel(WriteIndex[1]));
  Demultiplexer demultiplexer_15 (
    .out0(demultiplexer_15_out0), .out1(demultiplexer_15_out1), .in(demultiplexer_7_out1), .sel(WriteIndex[1]));
  Demultiplexer demultiplexer_16 (.out0(WS0), .out1(WS1), .in(demultiplexer_8_out0), .sel(WriteIndex[0]));
  Demultiplexer demultiplexer_17 (.out0(WS2), .out1(WS3), .in(demultiplexer_8_out1), .sel(WriteIndex[0]));
  Demultiplexer demultiplexer_18 (.out0(WS4), .out1(WS5), .in(demultiplexer_9_out0), .sel(WriteIndex[0]));
  Demultiplexer demultiplexer_19 (.out0(WS6), .out1(WS7), .in(demultiplexer_9_out1), .sel(WriteIndex[0]));
  Demultiplexer demultiplexer_20 (.out0(WS8), .out1(WS9), .in(demultiplexer_10_out0), .sel(WriteIndex[0]));
  Demultiplexer demultiplexer_21 (.out0(WS10), .out1(WS11), .in(demultiplexer_10_out1), .sel(WriteIndex[0]));
  Demultiplexer demultiplexer_22 (.out0(WS12), .out1(WS13), .in(demultiplexer_11_out0), .sel(WriteIndex[0]));
  Demultiplexer demultiplexer_23 (.out0(WS14), .out1(WS15), .in(demultiplexer_11_out1), .sel(WriteIndex[0]));
  Multiplexer #(.width(32)) multiplexer_57 (
    .in0(multiplexer_49_out), .in1(multiplexer_50_out), .out(multiplexer_57_out), .sel(ReadIndex1[3]));
  Multiplexer #(.width(32)) multiplexer_58 (
    .in0(multiplexer_51_out), .in1(multiplexer_52_out), .out(multiplexer_58_out), .sel(ReadIndex1[3]));
  Multiplexer #(.width(32)) multiplexer_59 (
    .in0(multiplexer_53_out), .in1(multiplexer_54_out), .out(multiplexer_59_out), .sel(ReadIndex2[3]));
  Multiplexer #(.width(32)) multiplexer_60 (
    .in0(multiplexer_55_out), .in1(multiplexer_56_out), .out(multiplexer_60_out), .sel(ReadIndex2[3]));
  Demultiplexer demultiplexer_24 (.out0(WS16), .out1(WS17), .in(demultiplexer_12_out0), .sel(WriteIndex[0]));
  Demultiplexer demultiplexer_25 (.out0(WS18), .out1(WS19), .in(demultiplexer_12_out1), .sel(WriteIndex[0]));
  Demultiplexer demultiplexer_26 (.out0(WS20), .out1(WS21), .in(demultiplexer_13_out0), .sel(WriteIndex[0]));
  Demultiplexer demultiplexer_27 (.out0(WS22), .out1(WS23), .in(demultiplexer_13_out1), .sel(WriteIndex[0]));
  Demultiplexer demultiplexer_28 (.out0(WS24), .out1(WS25), .in(demultiplexer_14_out0), .sel(WriteIndex[0]));
  Demultiplexer demultiplexer_29 (.out0(WS26), .out1(WS27), .in(demultiplexer_14_out1), .sel(WriteIndex[0]));
  Demultiplexer demultiplexer_30 (.out0(WS28), .out1(WS29), .in(demultiplexer_15_out0), .sel(WriteIndex[0]));
  Demultiplexer demultiplexer_31 (.out0(WS30), .out1(WS31), .in(demultiplexer_15_out1), .sel(WriteIndex[0]));
  Multiplexer #(.width(32)) multiplexer_61 (
    .in0(multiplexer_57_out), .in1(multiplexer_58_out), .out(ReadData1), .sel(ReadIndex1[4]));
  Multiplexer #(.width(32)) multiplexer_62 (
    .in0(multiplexer_59_out), .in1(multiplexer_60_out), .out(ReadData2), .sel(ReadIndex2[4]));

  // Other names for the same wires on the sheet: R10 = ReadIndex1[0]; R11 = ReadIndex1[1]; R12 = ReadIndex1[2];
  //   R13 = ReadIndex1[3]; R14 = ReadIndex1[4]; R20 = ReadIndex2[0]; R21 = ReadIndex2[1]; R22 = ReadIndex2[2];
  //   R23 = ReadIndex2[3]; R24 = ReadIndex2[4]; W0 = WriteIndex[0]; W1 = WriteIndex[1]; W2 = WriteIndex[2];
  //   W3 = WriteIndex[3]; W4 = WriteIndex[4]

  // Notes on the sheet:
  //   INPUTS to your circuit
  //   DON'T CHANGE THE LOCATIONS OF THE INPUTS AND OUTPUTS!
  //   These are DEBUG/TEST outputs from your circuit.
  //   OUTPUTS from your circuit
endmodule
